# Fritzing sketch skematic (saved by Fritzing 0.9.3b)
breadboards: 1

parts:
  U1 = ESP32-38PinWide [part_number=ESP32-38PinWide]
  M1 = MakerFocus MAX30102
  LCD1 = LCD screen
  LCM1602_IIC1 = LCM1602 IIC [part_number="LCM1602 IIC" chip_label="LCM1602 IIC" package="DIP (Dual Inline) [THT]"]
  LED1 = smd LED [color="Red (633nm)" package="1206 [SMD]"]
  Power_plug1 = Power plug
  J1 = Piezo Speaker
  R1 = Resistor [tolerance=±5% resistance=220 package=THT]
  LED2 = smd LED [color="Red (633nm)" package="1206 [SMD]"]
  R2 = Resistor [tolerance=±5% resistance=220 package=THT]
  U2 = SWITCH-SPST-2 [package=r_sw_th]
  U3 = SWITCH-SPST-2 [package=r_sw_th]

nets:
  N1: U1.3.3, U3.P
  GND: U1.GND, M1.GND, LCM1602_IIC1.GND, LED1.cathode, Power_plug1.GND, J1.pin1, LED2.cathode
  VIN: U1.VIN, LCM1602_IIC1.VCC, U2.O
  N2: U1.GPIO2, R2.Pin_0
  N3: U1.GPIO4, R1.Pin_0
  N4: U1.GPIO5, J1.pin2
  N5: U1.GPIO19, M1.INT
  N6: U1.GPIO21, M1.SDA, LCM1602_IIC1.SDA
  N7: U1.GPIO22, M1.SCL, LCM1602_IIC1.SCL
  N8: M1.VIN, U3.O
  VSS: LCD1.VSS, LCM1602_IIC1.VSS
  VDD: LCD1.VDD, LCM1602_IIC1.VDD
  N9: LCD1.V0, LCM1602_IIC1.V0
  N10: LCD1.RS, LCM1602_IIC1.RS
  N11: LCD1.R/W, LCM1602_IIC1.RW
  N12: LCD1.E, LCM1602_IIC1.E
  N13: LCD1.DB0, LCM1602_IIC1.D0
  N14: LCD1.DB1, LCM1602_IIC1.D1
  N15: LCD1.DB2, LCM1602_IIC1.D2
  N16: LCD1.DB3, LCM1602_IIC1.D3
  N17: LCD1.DB4, LCM1602_IIC1.D4
  N18: LCD1.DB5, LCM1602_IIC1.D5
  N19: LCD1.DB6, LCM1602_IIC1.D6
  N20: LCD1.DB7, LCM1602_IIC1.D7
  N21: LCD1.LED+, LCM1602_IIC1.A
  N22: LCD1.LED-, LCM1602_IIC1.K
  N23: LCM1602_IIC1.LED_A, LCM1602_IIC1.LED_B
  N24: LED1.anode, R1.Pin_1
  N25: Power_plug1.VCC, U2.P
  N26: LED2.anode, R2.Pin_1

custom parts:
  ESP32-38PinWide: Generic 38-Pin ESP32 with wide format (only access to one side of pins on a breadboard) based on Stephen Lilley's HiLetgo ESP-WROOM-32 ESP32 ESP-32S Development Board.
  MakerFocus MAX30102: Oximeter module using the MAX30102 chip. As usual, if you want the mounting holes in pcb, you need to drag a hole over the pad in silkscreen to actually drill the hole (by default they are not drilled)
  LCM1602 IIC: I2C-Module to use a 1602 or 2004 LCD on with the wire.h libory Serial LCD Modul
